# Fritzing sketch dispenser-with-just-resistors (saved by Fritzing 1.0.2b)
circuit board: 5.8cm x 4.5cm
breadboards: 1

parts:
  USB-ESP = Header 5x2 [package=2x5-ra]
  J1 = Basic Servo
  R20 = Resistor [tolerance=±20% power=0.25 resistance=47 package=THT]
  R21 = Resistor [tolerance=±20% power=0.25 resistance=47 package=THT]
  ESP32-30pin1 = LuaNode32 / ESP32 [part_number=ESP32S-PIN30]
  R23 = Trimmer Potentiometer [maximum_resistance=200Ω knob_status=50% power=0.5W package=THT]
  R24 = Trimmer Potentiometer [maximum_resistance=200Ω knob_status=50% power=0.5W package=THT]
  USB-S = Header 5x2 [package=2x5-ra]

nets (from the schematic view):
  GND: USB-ESP.1, J1.gnd, R20.Pin_1, ESP32-30pin1.GND, R23.wiper, USB-S.1
  N1: USB-ESP.9, ESP32-30pin1.Vin, R24.leg2
  N2: J1.pulse, ESP32-30pin1.D19
  N3: R20.Pin_0, R24.wiper
  N4: R21.Pin_1, R23.leg2

notes:
  resistor for servo. Servo doesn't take current at all in idle mode, so we need to take full 70mA through resistor
  Adding resistor to be able to adjust current taken.
  If resistor is set to 200R, then current is 25mA
  If resistor is set to 0, then additional current is 100mA
  resistor for esp32 circuit. I assume that esp32 takes 35mAh, so need to draw additional 35mAh
  also adding 200R resistor to be able to adjust current taken.

custom parts:
  LuaNode32 / ESP32: New Image for LuaNode32 DOIT ESP32 DEVKIT V1. Base parts from LuaNode32 / ESP32 ESP32 based LuaNode32 by G.Noorlander DOIT Esp32 DevKit v1 (30 pins long, 11 pins width) by Werner Rothschopf (modified by vanepp Dec 2018)
